# Fritzing sketch ExtendedFeedback (saved by Fritzing 0.9.1b)
breadboards: 1

parts:
  Componente1 = Arduino Uno (Rev3)
  S1 = Pushbutton [package="[THT]"]
  R1 = Resistor [tolerance=±5% resistance=10k package=THT]
  S2 = Pushbutton [package="[THT]"]
  R2 = Resistor [tolerance=±5% resistance=10k package=THT]
  S3 = Pushbutton [package="[THT]"]
  R3 = Resistor [tolerance=±5% resistance=10k package=THT]
  U1 = RF-LINK_TX [package=rf-link_tx]
  LCD1 = LCD screen
  U2 = POT [package=pot_alpha_rv16af-20]

nets:
  N1: Componente1.A0, U2.S
  N2: Componente1.D8, S3.Pin_1, S3.Pin_2, R3.Pin_0
  N3: Componente1.D11_PWM/MOSI, LCD1.E
  N4: Componente1.D12/MISO, LCD1.RS
  N5: Componente1.D0/RX, U1.+5V
  N6: Componente1.D1/TX, U1.ANT
  N7: Componente1.D2, LCD1.DB7
  N8: Componente1.D3_PWM, LCD1.DB6
  N9: Componente1.D4, LCD1.DB5
  N10: Componente1.D5_PWM, LCD1.DB4
  N11: Componente1.D6_PWM, S1.Pin_1, S1.Pin_2, R1.Pin_0
  N12: Componente1.D7, S2.Pin_1, S2.Pin_2, R2.Pin_0
  N13: Componente1.5V, S1.Pin_3, S1.Pin_4, S2.Pin_3, S2.Pin_4, S3.Pin_3, S3.Pin_4, U2.E
  N14: Componente1.GND, R1.Pin_1, R2.Pin_1, R3.Pin_1, U2.A
  N15: LCD1.VSS, LCD1.LED-
  N16: LCD1.VDD, LCD1.LED+

notes:
  Generic Bluetooth
  Previous
  Play/Pause
  Next
