# Fritzing sketch SimpleControlAndFrequencyBins (saved by Fritzing 0.9.1b)
breadboards: 1

parts:
  Componente1 = Arduino Uno (Rev3)
  S1 = Pushbutton [package="[THT]"]
  R1 = Resistor [tolerance=±5% resistance=10k package=THT]
  S2 = Pushbutton [package="[THT]"]
  R2 = Resistor [tolerance=±5% resistance=10k package=THT]
  S3 = Pushbutton [package="[THT]"]
  R3 = Resistor [tolerance=±5% resistance=10k package=THT]
  U1 = RF-LINK_TX [package=rf-link_tx]
  R4 = Resistor [tolerance=±5% resistance=1k package=THT]
  R5 = Resistor [tolerance=±5% resistance=1k package=THT]
  R6 = Resistor [tolerance=±5% resistance=1k package=THT]
  R7 = Resistor [tolerance=±5% resistance=1k package=THT]
  LED1 = LED - 5mm [color="Red (633nm)" package="5 mm [THT]"]
  LED2 = LED - 5mm [color="Red (633nm)" package="5 mm [THT]"]
  LED3 = LED - 5mm [color="Red (633nm)" package="5 mm [THT]"]
  LED4 = LED - 5mm [color="Red (633nm)" package="5 mm [THT]"]

nets:
  N1: Componente1.D9_PWM, R5.Pin_1
  N2: Componente1.D10_PWM/SS, R4.Pin_1
  N3: Componente1.D0/RX, U1.+5V
  N4: Componente1.D1/TX, U1.ANT
  N5: Componente1.D2, S3.Pin_1, S3.Pin_2, R3.Pin_0
  N6: Componente1.D3_PWM, S2.Pin_1, S2.Pin_2, R2.Pin_0
  N7: Componente1.D4, S1.Pin_1, S1.Pin_2, R1.Pin_0
  N8: Componente1.D5_PWM, R7.Pin_1
  N9: Componente1.D6_PWM, R6.Pin_1
  N10: Componente1.5V, S1.Pin_3, S1.Pin_4, S2.Pin_3, S2.Pin_4, S3.Pin_3, S3.Pin_4
  N11: Componente1.GND, R1.Pin_1, R2.Pin_1, R3.Pin_1, LED1.cathode, LED2.cathode, LED3.cathode, LED4.cathode
  N12: R4.Pin_0, LED1.anode
  N13: R5.Pin_0, LED2.anode
  N14: R6.Pin_0, LED3.anode
  N15: R7.Pin_0, LED4.anode

notes:
  5V
  GND
  Generic Bluetooth
  Previous
  Play/Pause
  Next
